# Fritzing sketch fall-detection-wiring (saved by Fritzing 0.9.3b)
breadboards: 1

parts:
  Part1 = InvenSense MPU6050
  A1 = Werner Rothschopf (modified to ESP32-S3-DevKitC dual USB by vanepp Aug 2024)
  Part2 = KY-006 Passive Buzzer Module [package="Breakout board"]

nets:
  N1: Part1.VCC, A1.Pin_1, A1.Pin_2
  N2: Part1.GND, A1.Pin_22, A1.Pin_23, A1.Pin_24, A1.Pin_44, Part2.-
  N3: Part1.SCL, A1.Pin_15
  N4: Part1.SDA, A1.Pin_12
  N5: A1.Pin_6, Part2.S

custom parts:
  Werner Rothschopf (modified to ESP32-S3-DevKitC dual USB by vanepp Aug 2024): ESP32-S3 ESP32-S3-DevKitC-1 Dual USB development board Pyboard CircuitPython Micropython wifi BLE5.0 ESP32-S3.
  KY-006 Passive Buzzer Module: Passive Piezoelectric Buzzer Module Keyes KY-006, it can produce a range of sound tones depending on the input frequency.
